# Fritzing sketch cookingProbe (saved by Fritzing 0.9.4)
circuit board: 10.1cm x 6.1cm
breadboards: 1

parts:
  Particle = Particle Argon
  Probe4 = Adafruit Thermocouple Amplifier with 1-Wire Breakout Board - MAX31850K [part_number="Adafruit #1727"]
  Probe3 = Adafruit Thermocouple Amplifier with 1-Wire Breakout Board - MAX31850K [part_number="Adafruit #1727"]
  Probe2 = Adafruit Thermocouple Amplifier with 1-Wire Breakout Board - MAX31850K [part_number="Adafruit #1727"]
  Probe1 = Adafruit Thermocouple Amplifier with 1-Wire Breakout Board - MAX31850K [part_number="Adafruit #1727"]
  R1 = Resistor [tolerance=±5% resistance=220 package=THT]
  Buzzer = Piezo Speaker
  Button = Pushbutton [package=THT]
  LCD_Out = female pin header, 4 pins [form="♀ (female)"]
  J1 = female pin header, 35 pins [form="♀ (female)"]

nets:
  VIN: Particle.3.3V, Probe4.VIN, Probe3.VIN, Probe2.VIN, Probe1.VIN, R1.Pin_0
  GND: Particle.GND, Probe4.GND, Probe3.GND, Probe2.GND, Probe1.GND, Buzzer.pin1, Button.leg1, LCD_Out.pin4, J1.pin1, J1.pin2, J1.pin3, J1.pin4, J1.pin5, J1.pin6, J1.pin7, J1.pin8, J1.pin9, J1.pin10, J1.pin11, J1.pin12, J1.pin13, J1.pin14, J1.pin15, J1.pin16, J1.pin17, J1.pin18, J1.pin19, J1.pin20, J1.pin21, J1.pin22, J1.pin23, J1.pin24, J1.pin25, J1.pin26, J1.pin27, J1.pin28, J1.pin29, J1.pin30, J1.pin31, J1.pin32, J1.pin33, J1.pin34, J1.pin35
  N1: Particle.A0, Button.leg0
  N2: Particle.A5, Buzzer.pin2
  N3: Particle.SDA, LCD_Out.pin1
  N4: Particle.SCL, LCD_Out.pin2
  N5: Particle.D4, Probe4.DATA, Probe3.DATA, Probe2.DATA, Probe1.DATA, R1.Pin_1
  N6: Particle.VUSB, LCD_Out.pin3

notes:
  KAGtronics
  KitchenTemp v2.0
  12/2020

custom parts:
  Particle Argon: The Argon is a powerful Wi-Fi enabled development board that can act as either a standalone Wi-Fi endpoint or Wi-Fi enabled gateway for Particle Mesh networks. It is based on the Nordic nRF52840 and has built-in battery charging circuitry so it’s easy to connect a Li-Po and deploy your local network in minutes. The Argon is great for connecting existing projects to the Particle Device Cloud or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
  Adafruit Thermocouple Amplifier with 1-Wire Breakout Board - MAX31850K: Thermocouples are very sensitive, requiring a good amplifier with a cold-compensation reference. So far we've carried the very nice MAX31855 which is an SPI interface thermocouple amplifier. The '855 is great but if you have a lot of thermocouples to measure it isn't terribly easy to use. That's why we are also carrying the new '850 model from Maxim - it's a "1-Wire" thermocouple amp which can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
